// Logisim project MUX Online.circ as structural Verilog: 1 circuit, main circuit main
module main (
  input  A,
  input  B,
  input  C,
  input  D,
  input  in_5,
  input  in_6,
  output out_7,
  output out_8
);

  wire not_1_out, not_2_out;

  not not_1 (not_1_out, C);
  not not_2 (not_2_out, D);
  // _74153 _4x1_MUX: pin names not known; wires that end beside it: D, not_2_out, not_1_out, A, in_5, in_5, not_2_out, in_6, out_8, 1'b0, 1'b1, C, B, D, not_2_out, D, not_2_out, out_7
endmodule
