// Logisim project Counter_Online.circ as structural Verilog: 1 circuit, main circuit main
module main (
  output out_1,
  output out_2,
  output out_3
);

  wire clock_1_out;

  Clock clock_1 (.out(clock_1_out));
  // _7476 T0: pin names not known; wires that end beside it: clock_1_out, 1'b1, 1'b1, 1'b1, 1'b1, out_1, 1'b0
  // _7476 T1: pin names not known; wires that end beside it: out_1, 1'b1, 1'b1, 1'b1, 1'b1, out_2, 1'b0
  // _7476 T2: pin names not known; wires that end beside it: out_2, 1'b1, 1'b1, 1'b1, 1'b1, out_3, 1'b0

  // Notes on the sheet:
  //   Asynchronus UP Counter Using T Flip Flop
endmodule
