// Logisim project 1.circ as structural Verilog: 1 circuit, main circuit 1
module _1 (
  input  J,
  input  K,
  output Q,
  output Q_prime
);

  wire CLK_out, n7400_1_p2, n7400_1_p3, n7400_1_p11, n7400_2_p3, n7400_2_p6, n7410_1_p9, n7410_1_p13;

  Clock CLK (.out(CLK_out));
  // _7410 7410_1: pin names not known; wires that end beside it: CLK_out, 1'b0, 1'b1, J, CLK_out, CLK_out, K, Q, n7410_1_p9, 1'b0, 1'b1, Q_prime, n7410_1_p13
  // _7400 7400_1: pin names not known; wires that end beside it: n7410_1_p13, n7400_1_p2, n7400_1_p3, n7410_1_p9, n7400_1_p3, n7400_1_p2, 1'b0, 1'b1, CLK_out, CLK_out, n7400_1_p11
  // _7400 7400_2: pin names not known; wires that end beside it: n7400_1_p3, n7400_1_p11, n7400_2_p3, n7400_1_p2, n7400_1_p11, n7400_2_p6, 1'b0, 1'b1, n7400_2_p3, Q_prime, Q, n7400_2_p6, Q, Q_prime
endmodule
