// Logisim project 1905079.circ as structural Verilog: 1 circuit, main circuit 2
module _2 (
  input  Clk,
  input  CLR,
  input  in_3,
  input  in_4,
  input  Serial_Input_Shift_Left,
  input  I1,
  input  I0,
  input  Serial_Input_Shift_Right,
  input  I3,
  input  S1,
  input  I2,
  input  S0,
  output A3,
  output A2,
  output A1,
  output A0
);

  wire n7474_1_p2, n7474_1_p9, n7474_2_p2, n7474_2_p9;

  // _7474 7474_1: pin names not known; wires that end beside it: CLR, n7474_1_p2, Clk, 1'b0, A3, 1'b0, 1'b1, CLR, n7474_1_p9, Clk, 1'b0, A2
  // _74153 74153_1: pin names not known; wires that end beside it: A3, in_4, S1, I3, A2, Serial_Input_Shift_Right, A3, n7474_1_p2, 1'b0, 1'b1, in_4, S0, I2, A1, A3, A2, n7474_1_p9, A2
  // _7474 7474_2: pin names not known; wires that end beside it: CLR, n7474_2_p2, Clk, 1'b0, A1, 1'b0, 1'b1, CLR, n7474_2_p9, Clk, A0
  // _74153 74153_2: pin names not known; wires that end beside it: A1, in_3, S1, I1, A0, A2, A1, n7474_2_p2, 1'b0, 1'b1, in_3, S0, I0, Serial_Input_Shift_Left, A1, A0, n7474_2_p9, A0
endmodule
